# Fritzing sketch SYC Proto 0A1 (saved by Fritzing 0.9.2b)
circuit board: 8.5cm x 6cm
breadboards: 1

parts:
  R6 = Resistor [tolerance=±5% resistance=150 package="0805 [SMD]"]
  Rain = female pin header, 2 pins [form="♀ (female)"]
  DS18b20 = mystery part, 3 pins [chip_label=DS18B20]
  Siren2b = Screw terminal - 2 pins [package=THT]
  12v = female pin header, 2 pins [form="♀ (female)"]
  U14 = Voltage Regulator - 5V [package="TO220 [THT]"]
  siren2a = Piezo Speaker
  siren_1 = Piezo Speaker
  Power_plug2 = Power plug
  R29 = Resistor [tolerance=±5% resistance=10k package="0805 [SMD]"]
  R31 = Resistor [tolerance=±5% resistance=10k package="0805 [SMD]"]
  Q22 = NPN-Transistor [package="SOT-23 [SMD]"]
  Q24 = NPN-Transistor [package="SOT-23 [SMD]"]
  5v = female pin header, 2 pins [form="♀ (female)"]
  C46 = Electrolytic Capacitor [capacitance=470µF package="200 mil [THT, electrolytic]"]
  Q2 = MOSFET-NCHANNEL [package=sot23-3]
  Q1 = MOSFET-NCHANNEL [package=sot23-3]
  Q3 = MOSFET-NCHANNEL [package=sot23-3]
  Q4 = MOSFET-NCHANNEL [package=sot23-3]
  R33 = Resistor [tolerance=±5% resistance=100 package="0805 [SMD]"]
  R38 = Resistor [tolerance=±5% resistance=10k package="0805 [SMD]"]
  R34 = Resistor [tolerance=±5% resistance=100 package="0805 [SMD]"]
  R39 = Resistor [tolerance=±5% resistance=10k package="0805 [SMD]"]
  R35 = Resistor [tolerance=±5% resistance=100 package="0805 [SMD]"]
  R37 = Resistor [tolerance=±5% resistance=10k package="0805 [SMD]"]
  R36 = Resistor [tolerance=±5% resistance=100 package="0805 [SMD]"]
  R40 = Resistor [tolerance=±5% resistance=10k package="0805 [SMD]"]
  Pad2 = Pad [width=4 height=3 connect=center]
  Pad3 = Pad [width=4 height=3 connect=center]
  Pad4 = Pad [width=4 height=3 connect=center]
  Pad5 = Pad [width=4 height=3 connect=center]
  C41 = Ceramic Capacitor [capacitance=220nF package="0805 [SMD, multilayer]"]
  C40 = Ceramic Capacitor [capacitance=100nF package="0805 [SMD, multilayer]"]
  Grow = smd LED [color="Red (633nm)" package="0805 [SMD]"]
  Fuse1 = Fuse with Handler [part_number=Htc-15m]
  D16 = Rectifier Diode [part_number=1N4001 package="Melf DO-213 AB [SMD]"]
  R25 = Resistor [tolerance=±20% resistance=4.7k package="0805 [SMD]"]
  C47 = Ceramic Capacitor [capacitance=100nF package="0805 [SMD, multilayer]"]
  Q5 = MOSFET-NCHANNEL [package=sot23-3]
  R41 = Resistor [tolerance=±5% resistance=100 package="0805 [SMD]"]
  R42 = Resistor [tolerance=±5% resistance=10k package="0805 [SMD]"]
  Particle = Spark Core (v1.0)
  Q6 = MOSFET-NCHANNEL [package=sot23-3]
  R43 = Resistor [tolerance=±5% resistance=100 package="0805 [SMD]"]
  R44 = Resistor [tolerance=±5% resistance=10k package="0805 [SMD]"]
  J1 = screw terminal, 8 pins
  V5 = smd LED [color="Red (633nm)" package="0805 [SMD]"]
  R45 = Resistor [tolerance=±5% resistance=150 package="0805 [SMD]"]
  V1 = smd LED [color="Green (565nm)" package="0805 [SMD]"]
  R46 = Resistor [tolerance=±5% resistance=150 package="0805 [SMD]"]
  V2 = smd LED [color="Green (560nm)" package="0805 [SMD]"]
  R47 = Resistor [tolerance=±5% resistance=150 package="0805 [SMD]"]
  V3 = smd LED [color="Green (555nm)" package="0805 [SMD]"]
  R48 = Resistor [tolerance=±5% resistance=150 package="0805 [SMD]"]
  V4 = smd LED [color="Green (555nm)" package="0805 [SMD]"]
  R49 = Resistor [tolerance=±5% resistance=150 package="0805 [SMD]"]
  Status = smd LED [color="Yellow (592nm)" package="0805 [SMD]"]
  R50 = Resistor [tolerance=±5% resistance=150 package="0805 [SMD]"]
  Rain_2 = smd LED [color="Blue (430nm)" package="0805 [SMD]"]
  R51 = Resistor [tolerance=±5% resistance=150 package="0805 [SMD]"]
  U15 = RJ45 Jack [package=rj45-8]
  Pad6 = Pad [width=4 height=3 connect=center]
  Pad7 = Pad [width=4 height=3 connect=center]
  Expansion = female pin header, 10 pins [form="♀ (female)"]  # not connected

nets:
  N1: R6.Pin_0, Grow.cathode
  GND: R6.Pin_1, DS18b20.pin3, 12v.pin2, U14.GND, Power_plug2.GND, Q22.2, Q24.2, 5v.pin2, C46.-, Q2.S, Q1.S, Q3.S, Q4.S, R38.Pin_0, R39.Pin_0, R37.Pin_0, R40.Pin_0, C41.0, C40.0, C47.0, Q5.S, R42.Pin_0, Particle.GND, Q6.S, R44.Pin_0, R45.Pin_1, R46.Pin_1, R47.Pin_1, R48.Pin_1, R49.Pin_1, R50.Pin_1, R51.Pin_1, U15.1
  Rain: Rain.pin1, Rain_2.anode, U15.6
  3v3: Rain.pin2, DS18b20.pin1, R25.Pin_1, Particle.3V3
  Temperature: DS18b20.pin2, R25.Pin_0, U15.3
  Siren2Out: Siren2b.pin1, siren2a.pin1, Q22.1
  12v: Siren2b.pin2, 12v.pin1, siren2a.pin2, siren_1.pin2, Fuse1.Connector2, D16.anode, J1.pin1
  N2: U14.input_voltage, C46.+, C41.1, D16.cathode
  5V/5v: U14.output_voltage, 5v.pin1, C40.1, C47.1, Particle.VIN
  Siren1Out: siren_1.pin1, Q24.1
  N3: Power_plug2.VCC, Fuse1.Connector1
  Siren2In: R29.Pin_0
  N4: R29.Pin_1, Q22.0
  Siren1In: R31.Pin_0
  N5: R31.Pin_1, Q24.0
  N6: Q2.G, R36.Pin_0
  V2out: Q2.D, Pad4.pad, J1.pin3
  N7: Q1.G, R35.Pin_0
  V1out: Q1.D, Pad3.pad, J1.pin2
  N8: Q3.G, R34.Pin_0
  V3out: Q3.D, Pad2.pad, J1.pin4
  N9: Q4.G, R33.Pin_0
  V4out: Q4.D, Pad5.pad, J1.pin5
  V4in: R33.Pin_1, R38.Pin_1, V4.anode
  V3in: R34.Pin_1, R39.Pin_1, V3.anode
  V1in: R35.Pin_1, R40.Pin_1, V1.anode
  V2in: R37.Pin_1, R36.Pin_1, V2.anode
  Growin: Grow.anode, R43.Pin_1, R44.Pin_1
  N10: Q5.G, R41.Pin_0
  V5out: Q5.D, J1.pin6, Pad6.pad
  V5in: R41.Pin_1, R42.Pin_1, V5.anode
  Tx: Particle.TX
  Rx: Particle.RX
  3v3*: Particle.3V3*, U15.2
  N11: Q6.G, R43.Pin_0
  Growout: Q6.D, J1.pin7, Pad7.pad
  N12: V5.cathode, R45.Pin_0
  N13: V1.cathode, R46.Pin_0
  N14: V2.cathode, R47.Pin_0
  N15: V3.cathode, R48.Pin_0
  N16: V4.cathode, R49.Pin_0
  N17: Status.cathode, R50.Pin_0
  Status: Status.anode
  N18: Rain_2.cathode, R51.Pin_0
  Light: U15.5

notes:
  - + 1 2 3 4 S
  Smart Room Controller, Full working version of Smart Home Controller. This variant intended for 5V use and with on-board voltage regulators., A1
  Grid Sizes:
  TQFP32: .125 mm
  Remainder:
  +
  -
